// Logisim project bus.circ as structural Verilog: 1 circuit, main circuit main
module main (
  input  in_1
);

  wire clock_1_out, shift_register_1_out, shift_register_1_q0, shift_register_1_q1, shift_register_1_q2,
       shift_register_1_q3, shift_register_1_q4, shift_register_1_q5, shift_register_1_q6;
  wire [7:0] ram_1_dout, random_1_out, random_2_out, register_1_q, register_2_q, shift_register_2_out,
       shift_register_2_q0, shift_register_2_q1, shift_register_2_q2, shift_register_2_q3,
       shift_register_2_q4, shift_register_2_q5, shift_register_2_q6, shift_register_2_q7,
       shift_register_2_q8, shift_register_2_q9, shift_register_2_q10, shift_register_2_q11,
       shift_register_2_q12, shift_register_2_q13, shift_register_2_q14, shift_register_2_q15,
       shift_register_2_q16, shift_register_2_q17, shift_register_2_q18, shift_register_2_q19,
       shift_register_2_q20, shift_register_2_q21, shift_register_2_q22, shift_register_2_q23,
       shift_register_2_q24, shift_register_2_q25, shift_register_2_q26, shift_register_2_q27,
       shift_register_2_q28, shift_register_2_q29, shift_register_2_q30, shift_register_2_q31,
       shift_register_2_q32, shift_register_2_q33, shift_register_2_q34, shift_register_2_q35,
       shift_register_2_q36, shift_register_2_q37, shift_register_2_q38, shift_register_2_q39,
       shift_register_2_q40, shift_register_2_q41, shift_register_2_q42, shift_register_2_q43,
       shift_register_2_q44, shift_register_2_q45, shift_register_2_q46, shift_register_2_q47,
       shift_register_2_q48, shift_register_2_q49, shift_register_2_q50, shift_register_2_q51,
       shift_register_2_q52, shift_register_2_q53, shift_register_2_q54, shift_register_2_q55,
       shift_register_2_q56, shift_register_2_q57, shift_register_2_q58, shift_register_2_q59,
       shift_register_2_q60, shift_register_2_q61, shift_register_2_q62;

  Shift_Register shift_register_1 (
    .in(shift_register_1_out), .clk(clock_1_out), .out(shift_register_1_out), .load(in_1), .d0(1'b0),
    .q0(shift_register_1_q0), .d1(1'b0), .q1(shift_register_1_q1), .d2(1'b0), .q2(shift_register_1_q2),
    .d3(1'b0), .q3(shift_register_1_q3), .d4(1'b1), .q4(shift_register_1_q4), .d5(1'b1),
    .q5(shift_register_1_q5), .d6(1'b1), .q6(shift_register_1_q6), .d7(1'b1));  // open: shift, clr, q7
  Clock clock_1 (.out(clock_1_out));
  DotMatrix #(.matrixcols(8), .matrixrows(1)) dotmatrix_1 (
    .col0(shift_register_1_q0), .col1(shift_register_1_q1), .col2(shift_register_1_q2),
    .col3(shift_register_1_q3), .col4(shift_register_1_q4), .col5(shift_register_1_q5),
    .col6(shift_register_1_q6), .col7(shift_register_1_out));
  Register register_1 (.D(random_2_out), .en(shift_register_1_q1), .clk(clock_1_out), .Q(register_1_q));  // open: clr
  Register register_2 (.D(random_1_out), .en(shift_register_1_q2), .clk(clock_1_out), .Q(register_2_q));  // open: clr
  Random random_1 (.next(shift_register_1_q3), .clk(clock_1_out), .out(random_1_out));  // open: clr
  Random random_2 (.next(shift_register_1_q4), .clk(clock_1_out), .out(random_2_out));  // open: clr
  RAM ram_1 (
    .addr(register_1_q), .we(shift_register_1_q0), .oe(shift_register_1_q5), .clk(clock_1_out),
    .din(register_2_q), .dout(ram_1_dout));
  Shift_Register #(.length(64), .width(8)) shift_register_2 (
    .shift(shift_register_1_q6), .in(ram_1_dout), .clk(clock_1_out), .out(shift_register_2_out),
    .d0(shift_register_2_out), .q0(shift_register_2_q0), .q1(shift_register_2_q1), .q2(shift_register_2_q2),
    .q3(shift_register_2_q3), .q4(shift_register_2_q4), .q5(shift_register_2_q5), .q6(shift_register_2_q6),
    .q7(shift_register_2_q7), .q8(shift_register_2_q8), .q9(shift_register_2_q9), .q10(shift_register_2_q10),
    .q11(shift_register_2_q11), .q12(shift_register_2_q12), .q13(shift_register_2_q13),
    .q14(shift_register_2_q14), .q15(shift_register_2_q15), .q16(shift_register_2_q16),
    .q17(shift_register_2_q17), .q18(shift_register_2_q18), .q19(shift_register_2_q19),
    .q20(shift_register_2_q20), .q21(shift_register_2_q21), .q22(shift_register_2_q22),
    .q23(shift_register_2_q23), .q24(shift_register_2_q24), .q25(shift_register_2_q25),
    .q26(shift_register_2_q26), .q27(shift_register_2_q27), .q28(shift_register_2_q28),
    .q29(shift_register_2_q29), .q30(shift_register_2_q30), .q31(shift_register_2_q31),
    .q32(shift_register_2_q32), .q33(shift_register_2_q33), .q34(shift_register_2_q34),
    .q35(shift_register_2_q35), .q36(shift_register_2_q36), .q37(shift_register_2_q37),
    .q38(shift_register_2_q38), .q39(shift_register_2_q39), .q40(shift_register_2_q40),
    .q41(shift_register_2_q41), .q42(shift_register_2_q42), .q43(shift_register_2_q43),
    .q44(shift_register_2_q44), .q45(shift_register_2_q45), .q46(shift_register_2_q46),
    .q47(shift_register_2_q47), .q48(shift_register_2_q48), .q49(shift_register_2_q49),
    .q50(shift_register_2_q50), .q51(shift_register_2_q51), .q52(shift_register_2_q52),
    .q53(shift_register_2_q53), .q54(shift_register_2_q54), .q55(shift_register_2_q55),
    .q56(shift_register_2_q56), .q57(shift_register_2_q57), .q58(shift_register_2_q58),
    .q59(shift_register_2_q59), .q60(shift_register_2_q60), .q61(shift_register_2_q61),
    .q62(shift_register_2_q62), .q63(shift_register_2_out));  // open: load, clr, d1, d2, d3, d4, d5, d6, d7, d8, d9, d10, d11, d12, d13, d14, d15, d16, d17, d18, d19, d20, d21, d22, d23, d24, d25, d26, d27, d28, d29, d30, d31, d32, d33, d34, d35, d36, d37, d38, d39, d40, d41, d42, d43, d44, d45, d46, d47, d48, d49, d50, d51, d52, d53, d54, d55, d56, d57, d58, d59, d60, d61, d62, d63
  DotMatrix #(.matrixcols(64), .matrixrows(8)) dotmatrix_2 (
    .col0(shift_register_2_q0), .col1(shift_register_2_q1), .col2(shift_register_2_q2),
    .col3(shift_register_2_q3), .col4(shift_register_2_q4), .col5(shift_register_2_q5),
    .col6(shift_register_2_q6), .col7(shift_register_2_q7), .col8(shift_register_2_q8),
    .col9(shift_register_2_q9), .col10(shift_register_2_q10), .col11(shift_register_2_q11),
    .col12(shift_register_2_q12), .col13(shift_register_2_q13), .col14(shift_register_2_q14),
    .col15(shift_register_2_q15), .col16(shift_register_2_q16), .col17(shift_register_2_q17),
    .col18(shift_register_2_q18), .col19(shift_register_2_q19), .col20(shift_register_2_q20),
    .col21(shift_register_2_q21), .col22(shift_register_2_q22), .col23(shift_register_2_q23),
    .col24(shift_register_2_q24), .col25(shift_register_2_q25), .col26(shift_register_2_q26),
    .col27(shift_register_2_q27), .col28(shift_register_2_q28), .col29(shift_register_2_q29),
    .col30(shift_register_2_q30), .col31(shift_register_2_q31), .col32(shift_register_2_q32),
    .col33(shift_register_2_q33), .col34(shift_register_2_q34), .col35(shift_register_2_q35),
    .col36(shift_register_2_q36), .col37(shift_register_2_q37), .col38(shift_register_2_q38),
    .col39(shift_register_2_q39), .col40(shift_register_2_q40), .col41(shift_register_2_q41),
    .col42(shift_register_2_q42), .col43(shift_register_2_q43), .col44(shift_register_2_q44),
    .col45(shift_register_2_q45), .col46(shift_register_2_q46), .col47(shift_register_2_q47),
    .col48(shift_register_2_q48), .col49(shift_register_2_q49), .col50(shift_register_2_q50),
    .col51(shift_register_2_q51), .col52(shift_register_2_q52), .col53(shift_register_2_q53),
    .col54(shift_register_2_q54), .col55(shift_register_2_q55), .col56(shift_register_2_q56),
    .col57(shift_register_2_q57), .col58(shift_register_2_q58), .col59(shift_register_2_q59),
    .col60(shift_register_2_q60), .col61(shift_register_2_q61), .col62(shift_register_2_q62),
    .col63(shift_register_2_out));

  // Other names for the same wires on the sheet: reset = in_1
endmodule
